# Fritzing sketch apple_controller (saved by Fritzing 0.8.3b)
breadboards: 1

parts:
  Part1 = Arduino Uno (Rev3)
  VS1838B = TSOP312.., 314.. [package=THT]

nets:
  N1: Part1.GND, VS1838B.Vs
  N2: Part1.D2, VS1838B.GND
  N3: Part1.5V, VS1838B.Data

notes:
  Vout GND Vcc
